// Digital circuit 16addressmemory.dig as structural Verilog
module _16addressmemory (
  input  [1:0] ctrl,
  input  [3:0] \input ,
  input  clk,
  input  [3:0] address,
  output [3:0] \output 
);

  wire and_1_out, and_2_out, and_3_out, and_4_out, and_5_out, and_6_out, and_7_out, and_8_out, and_9_out,
       and_10_out, and_11_out, and_12_out, and_13_out, and_14_out, and_15_out, and_16_out, decoder_1_out_0,
       decoder_1_out_1, decoder_1_out_2, decoder_1_out_3, decoder_1_out_4, decoder_1_out_5, decoder_1_out_6,
       decoder_1_out_7, decoder_1_out_8, decoder_1_out_9, decoder_1_out_10, decoder_1_out_11,
       decoder_1_out_12, decoder_1_out_13, decoder_1_out_14, decoder_1_out_15;
  wire [3:0] _4_bit_gpr_1_p4, _4_bit_gpr_2_p4, _4_bit_gpr_3_p4, _4_bit_gpr_4_p4, _4_bit_gpr_5_p4,
       _4_bit_gpr_6_p4, _4_bit_gpr_7_p4, _4_bit_gpr_8_p4, _4_bit_gpr_9_p4, _4_bit_gpr_10_p4,
       _4_bit_gpr_11_p4, _4_bit_gpr_12_p4, _4_bit_gpr_13_p4, _4_bit_gpr_14_p4, _4_bit_gpr_15_p4,
       _4_bit_gpr_16_p4;

  Decoder #(.Selector_Bits(4)) decoder_1 (
    .sel(address), .out_0(decoder_1_out_0), .out_1(decoder_1_out_1), .out_2(decoder_1_out_2),
    .out_3(decoder_1_out_3), .out_4(decoder_1_out_4), .out_5(decoder_1_out_5), .out_6(decoder_1_out_6),
    .out_7(decoder_1_out_7), .out_8(decoder_1_out_8), .out_9(decoder_1_out_9), .out_10(decoder_1_out_10),
    .out_11(decoder_1_out_11), .out_12(decoder_1_out_12), .out_13(decoder_1_out_13),
    .out_14(decoder_1_out_14), .out_15(decoder_1_out_15));
  and and_1 (and_1_out, clk, decoder_1_out_0);
  and and_2 (and_2_out, clk, decoder_1_out_1);
  and and_3 (and_3_out, clk, decoder_1_out_2);
  and and_4 (and_4_out, clk, decoder_1_out_3);
  and and_5 (and_5_out, clk, decoder_1_out_4);
  and and_6 (and_6_out, clk, decoder_1_out_5);
  and and_7 (and_7_out, clk, decoder_1_out_6);
  and and_8 (and_8_out, clk, decoder_1_out_7);
  and and_9 (and_9_out, clk, decoder_1_out_8);
  and and_10 (and_10_out, clk, decoder_1_out_9);
  and and_11 (and_11_out, clk, decoder_1_out_10);
  and and_12 (and_12_out, clk, decoder_1_out_11);
  and and_13 (and_13_out, clk, decoder_1_out_12);
  and and_14 (and_14_out, clk, decoder_1_out_13);
  and and_15 (and_15_out, clk, decoder_1_out_14);
  and and_16 (and_16_out, clk, decoder_1_out_15);
  // _4_bit_gpr _4_bit_gpr_1: pin names not known; wires that end beside it: ctrl, \input , and_1_out, _4_bit_gpr_1_p4
  // _4_bit_gpr _4_bit_gpr_2: pin names not known; wires that end beside it: ctrl, \input , and_2_out, _4_bit_gpr_2_p4
  // _4_bit_gpr _4_bit_gpr_3: pin names not known; wires that end beside it: ctrl, \input , and_3_out, _4_bit_gpr_3_p4
  // _4_bit_gpr _4_bit_gpr_4: pin names not known; wires that end beside it: ctrl, \input , and_4_out, _4_bit_gpr_4_p4
  // _4_bit_gpr _4_bit_gpr_5: pin names not known; wires that end beside it: ctrl, \input , and_5_out, _4_bit_gpr_5_p4
  // _4_bit_gpr _4_bit_gpr_6: pin names not known; wires that end beside it: ctrl, \input , and_6_out, _4_bit_gpr_6_p4
  // _4_bit_gpr _4_bit_gpr_7: pin names not known; wires that end beside it: ctrl, \input , and_7_out, _4_bit_gpr_7_p4
  // _4_bit_gpr _4_bit_gpr_8: pin names not known; wires that end beside it: ctrl, \input , and_8_out, _4_bit_gpr_8_p4
  // _4_bit_gpr _4_bit_gpr_9: pin names not known; wires that end beside it: ctrl, \input , and_9_out, _4_bit_gpr_9_p4
  // _4_bit_gpr _4_bit_gpr_10: pin names not known; wires that end beside it: ctrl, \input , and_10_out, _4_bit_gpr_10_p4
  // _4_bit_gpr _4_bit_gpr_11: pin names not known; wires that end beside it: ctrl, \input , and_11_out, _4_bit_gpr_11_p4
  // _4_bit_gpr _4_bit_gpr_12: pin names not known; wires that end beside it: ctrl, \input , and_12_out, _4_bit_gpr_12_p4
  // _4_bit_gpr _4_bit_gpr_13: pin names not known; wires that end beside it: ctrl, \input , and_13_out, _4_bit_gpr_13_p4
  // _4_bit_gpr _4_bit_gpr_14: pin names not known; wires that end beside it: ctrl, \input , and_14_out, _4_bit_gpr_14_p4
  // _4_bit_gpr _4_bit_gpr_15: pin names not known; wires that end beside it: ctrl, \input , and_15_out, _4_bit_gpr_15_p4
  // _4_bit_gpr _4_bit_gpr_16: pin names not known; wires that end beside it: ctrl, \input , and_16_out, _4_bit_gpr_16_p4
  Multiplexer #(.Selector_Bits(4), .Bits(4)) multiplexer_1 (
    .sel(address), .in_0(_4_bit_gpr_1_p4), .in_1(_4_bit_gpr_2_p4), .in_2(_4_bit_gpr_3_p4),
    .in_3(_4_bit_gpr_4_p4), .in_4(_4_bit_gpr_5_p4), .in_5(_4_bit_gpr_6_p4), .in_6(_4_bit_gpr_7_p4),
    .in_7(_4_bit_gpr_8_p4), .in_8(_4_bit_gpr_9_p4), .in_9(_4_bit_gpr_10_p4), .in_10(_4_bit_gpr_11_p4),
    .in_11(_4_bit_gpr_12_p4), .in_12(_4_bit_gpr_13_p4), .in_13(_4_bit_gpr_14_p4), .in_14(_4_bit_gpr_15_p4),
    .in_15(_4_bit_gpr_16_p4), .out(\output ));
endmodule
