// Digital circuit 4_bit_processor.dig as structural Verilog
module _4_bit_processor (
  input  clk,
  input  [1:0] IR_ctrl,
  input  [1:0] MEM_ctrl,
  input  [3:0] MEM_input,
  input  [1:0] PC_ctrl,
  output [15:0] instructions_16bit,
  output [3:0] ALU_output,
  output [3:0] data_1_out,
  output [3:0] data_2_out
);

  wire [7:0] registerfile_write_ctrl_1_p2;

  intrusction_memory_module intrusction_memory_module_1 (
    .IR_ctrl(IR_ctrl), .PC_ctrl(PC_ctrl), .Mem_ctrl(MEM_ctrl), .Mem_input(MEM_input), .clk(clk),
    .\output (instructions_16bit));
  // registerFile_write_ctrl registerfile_write_ctrl_1: pin names not known; wires that end beside it: instructions_16bit[1:0], registerfile_write_ctrl_1_p2
  _4_bit_register_file _4_bit_register_file_1 (
    .select_read1(instructions_16bit[5:4]), .select_read2(instructions_16bit[3:2]), .clk(clk),
    .write_data(ALU_output), .select_write(instructions_16bit[1:0]),
    .ctrl_registers(registerfile_write_ctrl_1_p2), .read_data_1(data_1_out), .read_data_2(data_2_out));
  _4_bit_alu _4_bit_alu_1 (
    .A(data_1_out), .B(data_2_out), .C_in_S_1_S_0(instructions_16bit[8:6]), .D(ALU_output));  // open: overflow

  // Notes on the sheet:
  //   PC_ctrl: default 1
endmodule

/* Test case test-circut:
IR_ctrl MEM_ctrl MEM_input PC_ctrl clk ALU_output data-1-out data-2-out
0 1 1 1 c x x x 
0 1 2 1 c x x x
0 1 3 1 c x x x 
0 1 4 1 c x x x 
0 1 5 1 c x x x 
0 1 6 1 c x x x 
0 1 7 1 c x x x 
1 0 0 1 c x x x
*/
