// Digital circuit 4_bit_register_file.dig as structural Verilog
module _4_bit_register_file (
  input  [1:0] select_read1,
  input  [1:0] select_read2,
  input  clk,
  input  [3:0] write_data,
  input  [1:0] select_write,
  input  [7:0] ctrl_registers,
  output [3:0] read_data_1,
  output [3:0] read_data_2
);

  wire [3:0] demultiplexer_1_out_0, demultiplexer_1_out_1, demultiplexer_1_out_2, demultiplexer_1_out_3,
       R_0_p4, R_1_p4, R_2_p4, R_3_p4;

  Demultiplexer #(.Bits(4), .Selector_Bits(2)) demultiplexer_1 (
    .sel(select_write), .in(write_data), .out_0(demultiplexer_1_out_0), .out_1(demultiplexer_1_out_1),
    .out_2(demultiplexer_1_out_2), .out_3(demultiplexer_1_out_3));
  // _4_bit_gpr R_0: pin names not known; wires that end beside it: ctrl_registers[1:0], demultiplexer_1_out_0, clk, R_0_p4
  // _4_bit_gpr R_1: pin names not known; wires that end beside it: ctrl_registers[3:2], demultiplexer_1_out_1, clk, R_1_p4
  // _4_bit_gpr R_2: pin names not known; wires that end beside it: ctrl_registers[5:4], demultiplexer_1_out_2, clk, R_2_p4
  // _4_bit_gpr R_3: pin names not known; wires that end beside it: ctrl_registers[7:6], demultiplexer_1_out_3, clk, R_3_p4
  Multiplexer #(.Bits(4), .Selector_Bits(2)) multiplexer_1 (
    .sel(select_read1), .in_0(R_0_p4), .in_1(R_1_p4), .in_2(R_2_p4), .in_3(R_3_p4), .out(read_data_1));
  Multiplexer #(.Selector_Bits(2), .Bits(4)) multiplexer_2 (
    .sel(select_read2), .in_0(R_0_p4), .in_1(R_1_p4), .in_2(R_2_p4), .in_3(R_3_p4), .out(read_data_2));
endmodule
