// Digital circuit 4bit_program_counter.dig as structural Verilog
module _4bit_program_counter (
  input  clk,
  input  [1:0] ctrl__inc__reset__load,
  output [3:0] \output 
);

  wire [3:0] _4bitadder_1_p3, multiplexer_1_out, not_1_out;

  // _4bitadder _4bitadder_1: pin names not known; wires that end beside it: 4'b0001, \output , _4bitadder_1_p3
  assign not_1_out = ~4'b0000;  // Not not_1, 4 bits wide
  Multiplexer #(.Selector_Bits(2), .Bits(4)) multiplexer_1 (
    .sel(ctrl__inc__reset__load), .in_0(\output ), .in_1(_4bitadder_1_p3), .in_2(4'b0000), .in_3(not_1_out),
    .out(multiplexer_1_out));
  D_FF d_ff_1 (.D(multiplexer_1_out[3]), .C(clk), .Q(\output [3]));  // open: nQ
  D_FF d_ff_2 (.D(multiplexer_1_out[2]), .C(clk), .Q(\output [2]));  // open: nQ
  D_FF d_ff_3 (.D(multiplexer_1_out[1]), .C(clk), .Q(\output [1]));  // open: nQ
  D_FF d_ff_4 (.D(multiplexer_1_out[0]), .C(clk), .Q(\output [0]));  // open: nQ
endmodule
