// Digital circuit intrusction_memory_module.dig as structural Verilog
module intrusction_memory_module (
  input  [1:0] IR_ctrl,
  input  [1:0] PC_ctrl,
  input  [1:0] Mem_ctrl,
  input  [3:0] Mem_input,
  input  clk,
  output [15:0] \output 
);

  wire and_1_out, not_1_out, not_2_out;
  wire [1:0] demultiplexer_1_out_0, demultiplexer_1_out_1, demultiplexer_1_out_2, demultiplexer_1_out_3;
  wire [3:0] _4bit_instruction_register_1_p4, _4bit_instruction_register_2_p4,
       _4bit_instruction_register_3_p4, _4bit_instruction_register_4_p4, _4bit_program_counter_1_output,
       _16addressmemory_1_output, demultiplexer_2_out_0, demultiplexer_2_out_1, demultiplexer_2_out_2,
       demultiplexer_2_out_3;

  _4bit_program_counter _4bit_program_counter_1 (
    .clk(clk), .ctrl__inc__reset__load(PC_ctrl), .\output (_4bit_program_counter_1_output));
  _16addressmemory _16addressmemory_1 (
    .ctrl(Mem_ctrl), .\input (Mem_input), .clk(clk), .address(_4bit_program_counter_1_output),
    .\output (_16addressmemory_1_output));
  Demultiplexer #(.Selector_Bits(2), .Bits(2)) demultiplexer_1 (
    .sel(_4bit_program_counter_1_output[1:0]), .in(IR_ctrl), .out_0(demultiplexer_1_out_0),
    .out_1(demultiplexer_1_out_1), .out_2(demultiplexer_1_out_2), .out_3(demultiplexer_1_out_3));
  not not_1 (not_1_out, _4bit_program_counter_1_output[0]);
  not not_2 (not_2_out, _4bit_program_counter_1_output[1]);
  Demultiplexer #(.Selector_Bits(2), .Bits(4)) demultiplexer_2 (
    .sel(_4bit_program_counter_1_output[1:0]), .in(_16addressmemory_1_output), .out_0(demultiplexer_2_out_0),
    .out_1(demultiplexer_2_out_1), .out_2(demultiplexer_2_out_2), .out_3(demultiplexer_2_out_3));
  and and_1 (and_1_out, not_1_out, not_2_out);
  // _4bit_instruction_register _4bit_instruction_register_1: pin names not known; wires that end beside it: demultiplexer_2_out_0, demultiplexer_1_out_0, clk, _4bit_instruction_register_1_p4
  // _4bit_instruction_register _4bit_instruction_register_2: pin names not known; wires that end beside it: demultiplexer_2_out_1, demultiplexer_1_out_1, clk, _4bit_instruction_register_2_p4
  // _4bit_instruction_register _4bit_instruction_register_3: pin names not known; wires that end beside it: demultiplexer_2_out_2, demultiplexer_1_out_2, clk, _4bit_instruction_register_3_p4
  // _4bit_instruction_register _4bit_instruction_register_4: pin names not known; wires that end beside it: demultiplexer_2_out_3, demultiplexer_1_out_3, clk, _4bit_instruction_register_4_p4
  assign \output  = and_1_out ? {_4bit_instruction_register_4_p4, _4bit_instruction_register_3_p4, _4bit_instruction_register_2_p4, _4bit_instruction_register_1_p4} : 16'bz;  // Driver driver_1

  // Notes on the sheet:
  //   PC_ctrl: default 1
  //   Mem_ctrl: default 1
endmodule
